# Fritzing sketch blinky-badge (saved by Fritzing 0.9.1b)
circuit board: 4cm x 4cm

parts:
  T2 = NPN-Transistor [part_number=BC547 package="TO92 [THT]"]
  R3 = Resistor [tolerance=±5% resistance=47k package=THT]
  R4 = Resistor [tolerance=±5% resistance=47k package=THT]
  R1 = Resistor [tolerance=±5% resistance=100k package=THT]
  C1 = Electrolytic Capacitor [capacitance=22µF package="100 mil [THT, electrolytic]"]
  C2 = Electrolytic Capacitor [capacitance=22µF package="100 mil [THT, electrolytic]"]
  T3 = NPN-Transistor [part_number=2N2222 package="TO92 [THT]"]
  T4 = NPN-Transistor [part_number=2N2222 package="TO92 [THT]"]
  R2 = Resistor [tolerance=±5% resistance=100 package=THT]
  R5 = Resistor [tolerance=±5% resistance=100 package=THT]
  LED1 = LED - 5mm [color="Red (633nm)" package="5 mm [THT]"]
  LED2 = LED - 5mm [color="Red (633nm)" package="5 mm [THT]"]
  T1 = NPN-Transistor [part_number=BC547 package="TO92 [THT]"]
  U1 = Touch Plate
  BAT1 = Battery Holders [package=battcom_20mm_pth]

nets:
  GND: T2.E, BAT1.-
  N1: T2.B, T1.E
  N2: T2.C, T3.E, T4.E, T1.C
  N3: R3.Pin_0, C1.-, T4.B
  N4: R3.Pin_1, R4.Pin_1, LED1.anode, LED2.anode, U1.T1, BAT1.+
  N5: R4.Pin_0, C2.-, T3.B
  N6: R1.Pin_0, U1.T2
  N7: R1.Pin_1, T1.B
  N8: C1.+, T3.C, R2.Pin_0
  N9: C2.+, T4.C, R5.Pin_0
  N10: R2.Pin_1, LED1.cathode
  N11: R5.Pin_1, LED2.cathode

notes:
  electronut.in
  Blinky Badge 1.0
  Touch activated LED Blinky Badge, 1.0

custom parts:
  Touch Plate: Electrode for resistive touch detection
